// Logisim project cpu.circ as structural Verilog: 14 circuits, main circuit main
module main (
  input  in_1,
  input  in_2,
  input  in_3,
  input  in_4,
  input  in_5,
  input  in_6,
  input  in_7,
  input  in_8,
  input  in_9,
  input  in_10,
  input  in_11,
  input  in_12,
  input  in_13,
  input  in_14,
  input  in_15,
  input  in_16,
  input  in_17,
  input  in_18,
  input  in_19,
  input  in_20,
  input  in_21,
  input  in_22,
  input  in_23,
  input  in_24,
  input  in_25,
  input  in_26,
  input  in_27,
  input  in_28,
  input  in_29,
  input  [7:0] in_30,
  input  [7:0] in_31,
  input  in_32,
  input  [5:0] in_33,
  output [7:0] out_34
);

  wire alu_1_c, alu_1_p, alu_1_v, alu_1_z, and_1_out, and_2_out, bCLK, bnCLK, button_1_out, CLK, COLDRESET,
       D1, D2, D3, D4, d_ff_1_q, d_ff_2_q, d_ff_2_qn, d_ff_3_q, d_ff_4_q, d_ff_5_q, d_ff_5_qn, d_ff_6_q,
       DISPLAYCLK, fCLK, nCLK, not_1_out, nRESET, or_2_out, or_3_out, PCclr, PCout, PRGMODE, PRM, T0, T1, T2,
       T3, T4, T5, undriven_2, WARMRESET;
  wire [3:0] counter_1_q_2, s1h, s1l, s2h, s2l, s3h, s3l, s4h, s4l, undriven;
  wire [7:0] DBUS, HEX;
  wire [11:0] counter_1_q;
  wire [15:0] A16BUS;

  Clock clock_1 (.out(DISPLAYCLK));
  assign CLK = 1'b1 ? DISPLAYCLK : 1'bz;  // Controlled_Buffer controlled_buffer_1
  assign nCLK = 1'b1 ? ~DISPLAYCLK : 1'bz;  // Controlled_Inverter cc
  Hex_Digit_Display hex_digit_display_1 (.value(counter_1_q_2));  // open: dp
  Counter #(.width(16), .max('hffff)) counter_1 (
    .load(in_28), .D(A16BUS), .count(fCLK), .Q({counter_1_q_2, counter_1_q}), .clk(fCLK), .clr(PCclr));  // open: carry
  ringcounter RING (.clk(fCLK), .clr(PCclr), .Q({T5, T4, T3, T2, T1, T0}));
  Hex_Digit_Display hex_digit_display_2 (.value(counter_1_q[11:8]));  // open: dp
  Hex_Digit_Display hex_digit_display_3 (.value(counter_1_q[7:4]));  // open: dp
  assign A16BUS = PCout ? {counter_1_q_2, counter_1_q} : 16'bz;  // Controlled_Buffer controlled_buffer_2
  displaycounter displaycounter_1 (.clk(DISPLAYCLK), .clr(PCclr), .Q({D4, D3, D2, D1}));
  decimaldisplay decimaldisplay_1 (.clk(DISPLAYCLK), .reset(PCclr), .digit(undriven));
  not not_1 (not_1_out, PRM);
  Hex_Digit_Display hex_digit_display_4 (.value(counter_1_q[3:0]));  // open: dp
  Button button_1 (.out(button_1_out));
  LED led_1 (.in(button_1_out));
  not not_2 (nRESET, PCclr);
  or or_1 (PCclr, WARMRESET, COLDRESET);
  and and_1 (and_1_out, PRGMODE, not_1_out);
  LED led_2 (.in(and_2_out));
  // Probe on {4'b0000, D4, D3, D2, D1, A16BUS[7:0]}
  and and_2 (and_2_out, PRGMODE, PRM);
  D_Flip_Flop d_ff_1 (.clk(DISPLAYCLK), .D(button_1_out), .Q(d_ff_1_q));  // open: Qn, preset, en, reset
  RAM ram_1 (.addr(A16BUS[7:0]), .data(DBUS), .sel(undriven_2), .clk(bCLK), .ld(or_2_out));  // open: clr
  or or_2 (or_2_out, PCout, and_1_out);
  assign A16BUS = PRGMODE ? {in_2, in_3, in_4, in_5, in_6, in_7, in_8, in_9, in_10, in_11, in_12, in_13, in_14, in_15, in_16, in_17} : 16'bz;  // Controlled_Buffer controlled_buffer_3
  assign DBUS = and_2_out ? {in_18, in_19, in_20, in_21, in_22, in_23, in_24, in_25} : 8'bz;  // Controlled_Buffer controlled_buffer_4
  D_Flip_Flop d_ff_2 (.clk(DISPLAYCLK), .D(d_ff_1_q), .Q(d_ff_2_q), .Qn(d_ff_2_qn));  // open: preset, en, reset
  Decoder #(.select(2)) decoder_1 (.out0(PCout), .out1(PRGMODE), .sel({in_27, in_26}));  // open: out2, out3, en
  D_Flip_Flop d_ff_3 (.clk(DISPLAYCLK), .D(d_ff_2_qn), .Q(d_ff_3_q));  // open: Qn, preset, en, reset
  ROM #(.addrWidth(16)) rom_1 (.addr({4'b0000, D4, D3, D2, D1, A16BUS[7:0]}), .data(HEX), .sel(1'b1));
  Multiplexer multiplexer_1 (.in0(CLK), .in1(bCLK), .out(fCLK), .sel(or_3_out));  // open: en
  or or_3 (or_3_out, in_29, PRGMODE);
  and and_3 (WARMRESET, d_ff_2_q, d_ff_3_q);
  not not_3 (COLDRESET, d_ff_3_q);
  // Probe on A16BUS[7:0]
  Hex_Digit_Display hex_digit_display_5 (.value(DBUS[7:4]));  // open: dp
  Hex_Digit_Display hex_digit_display_6 (.value(DBUS[3:0]));  // open: dp
  Hex_Digit_Display hex_digit_display_7 (.value({in_6, in_7, in_8, in_9}));  // open: dp
  Hex_Digit_Display hex_digit_display_8 (.value({in_2, in_3, in_4, in_5}));  // open: dp
  // Probe on HEX
  Hex_Digit_Display hex_digit_display_9 (.value({in_10, in_11, in_12, in_13}));  // open: dp
  Button button_2 (.out(PRM));
  LED led_3 (.in(PRM));
  alu alu_1 (
    .fn(in_33), .B(in_31), .C(alu_1_c), .A(in_30), .cin(in_32), .res(out_34), .Z(alu_1_z), .P(alu_1_p),
    .V(alu_1_v), .en(1'b1));
  Hex_Digit_Display hex_digit_display_10 (.value(A16BUS[15:12]));  // open: dp
  Hex_Digit_Display hex_digit_display_11 (.value({in_14, in_15, in_16, in_17}));  // open: dp
  D_Flip_Flop d_ff_4 (.clk(CLK), .D(PRM), .Q(d_ff_4_q));  // open: Qn, preset, en, reset
  LED led_4 (.in(alu_1_c));
  LED led_5 (.in(alu_1_z));
  LED led_6 (.in(alu_1_p));
  LED led_7 (.in(alu_1_v));
  _7_Segment_Display u_7_segment_display_1 (
    .g(s3h[3]), .f(s3h[2]), .a(s3h[1]), .b(s3h[0]), .e(s3l[3]), .d(s3l[2]), .c(s3l[1]), .dp(s3l[0]));
  _7_Segment_Display u_7_segment_display_2 (
    .g(s4h[3]), .f(s4h[2]), .a(s4h[1]), .b(s4h[0]), .e(s4l[3]), .d(s4l[2]), .c(s4l[1]), .dp(s4l[0]));
  _8bitbuffer u_8bitbuffer_1 (.I(HEX), .O({s1h, s1l}), .en(D1));
  _8bitbuffer u_8bitbuffer_2 (.I(HEX), .O({s3h, s3l}), .en(D3));
  Hex_Digit_Display hex_digit_display_12 (.value(A16BUS[11:8]));  // open: dp
  Hex_Digit_Display hex_digit_display_13 (.value(A16BUS[7:4]));  // open: dp
  D_Flip_Flop d_ff_5 (.clk(CLK), .D(d_ff_4_q), .Q(d_ff_5_q), .Qn(d_ff_5_qn));  // open: preset, en, reset
  _7_Segment_Display u_7_segment_display_3 (
    .g(s2h[3]), .f(s2h[2]), .a(s2h[1]), .b(s2h[0]), .e(s2l[3]), .d(s2l[2]), .c(s2l[1]), .dp(s2l[0]));
  Hex_Digit_Display hex_digit_display_14 (.value(A16BUS[3:0]));  // open: dp
  Hex_Digit_Display hex_digit_display_15 (.value({in_18, in_19, in_20, in_21}));  // open: dp
  Hex_Digit_Display hex_digit_display_16 (.value({in_22, in_23, in_24, in_25}));  // open: dp
  _7_Segment_Display u_7_segment_display_4 (
    .g(s1h[3]), .f(s1h[2]), .a(s1h[1]), .b(s1h[0]), .e(s1l[3]), .d(s1l[2]), .c(s1l[1]), .dp(s1l[0]));
  D_Flip_Flop d_ff_6 (.clk(CLK), .D(d_ff_5_qn), .Q(d_ff_6_q));  // open: Qn, preset, en, reset
  _8bitbuffer u_8bitbuffer_3 (.I(HEX), .O({s2h, s2l}), .en(D2));
  _8bitbuffer u_8bitbuffer_4 (.I(HEX), .O({s4h, s4l}), .en(D4));
  and and_4 (bCLK, d_ff_5_q, d_ff_6_q);
  not not_4 (bnCLK, bCLK);

  // Other names for the same wires on the sheet: DAB0[3:0] = {in_14, in_15, in_16, in_17};
  //   DAB1[3:0] = {in_10, in_11, in_12, in_13}; DAB2[3:0] = {in_6, in_7, in_8, in_9};
  //   DAB3[3:0] = {in_2, in_3, in_4, in_5}; DAD0[3:0] = {in_22, in_23, in_24, in_25};
  //   DAD1[3:0] = {in_18, in_19, in_20, in_21}; AL8BUS[7:0] = A16BUS[7:0]; AH8BUS[7:0] = A16BUS[15:8]; INCPC = fCLK;
  //   MAINCLK = DISPLAYCLK; PCLoad = in_28; RESET = PCclr

  // Notes on the sheet:
  //   contents of rom_1 (hex, n*v repeats v):
  //   256*0 7e 12 bc b6 d2 e6 ee 32 fe f2 7e 12 bc b6 d2 e6 ee 32 fe f2 7e 12 bc b6 d2 e6 ee 32 fe f2 7e
  //   12 bc b6 d2 e6 ee 32 fe f2 7e 12 bc b6 d2 e6 ee 32 fe f2 7e 12 bc b6 d2 e6 ee 32 fe f2 7e 12 bc b6
  //   d2 e6 ee 32 fe f2 7e 12 bc b6 d2 e6 ee 32 fe f2 7e 12 bc b6 d2 e6 ee 32 fe f2 7e 12 bc b6 d2 e6 ee
  //   32 fe f2 7e 12 bc b6 d2 e6 ee 32 fe f2 7e 12 bc b6 d2 e6 ee 32 fe f2 7e 12 bc b6 d2 e6 ee 32 fe f2
  //   7e 12 bc b6 d2 e6 ee 32 fe f2 7e 12 bc b6 d2 e6 ee 32 fe f2 7e 12 bc b6 d2 e6 ee 32 fe f2 7e 12 bc
  //   b6 d2 e6 ee 32 fe f2 7e 12 bc b6 d2 e6 ee 32 fe f2 7e 12 bc b6 d2 e6 ee 32 fe f2 7e 12 bc b6 d2 e6
  //   ee 32 fe f2 7e 12 bc b6 d2 e6 ee 32 fe f2 7e 12 bc b6 d2 e6 ee 32 fe f2 7e 12 bc b6 d2 e6 ee 32 fe
  //   f2 7e 12 bc b6 d2 e6 ee 32 fe f2 7e 12 bc b6 d2 e6 ee 32 fe f2 7e 12 bc b6 d2 e6 10*0 10*12 10*bc
  //   10*b6 10*d2 10*e6 10*ee 10*32 10*fe 10*f2 10*7e 10*12 10*bc 10*b6 10*d2 10*e6 10*ee 10*32 10*fe
  //   10*f2 10*7e 10*12 10*bc 10*b6 10*d2 6*e6 6*1 10*ff 340*0 100*12 56*bc
endmodule

// ALU
module alu (
  input  cin,
  input  [7:0] A,
  input  [7:0] B,
  input  en,
  input  [5:0] fn,
  output [7:0] res,
  output C,
  output Z,
  output P,
  output V
);

  wire and_2_out, and_3_out, and_4_out, cia, coa, cos, not_1_out, not_2_out, not_3_out, not_shift,
       Subtract_Function;
  wire [3:0] or_1_out;
  wire [7:0] adder_1_s, logic_1_res, shift_1_res;

  \logic  logic_1 (.B(B), .A(A), .lfnc(fn[3:0]), .Res(logic_1_res));
  not not_1 (not_1_out, fn[2]);
  not not_2 (not_2_out, fn[3]);
  shift shift_1 (.sfn(fn[5:4]), .cout(cos), .A(A), .res(shift_1_res), .cin(cin));
  xnor xnor_1 (not_shift, fn[4], fn[5]);
  and and_1 (Subtract_Function, fn[0], fn[1], not_1_out, not_2_out);
  adder adder_1 (.A(shift_1_res), .B(logic_1_res), .S(adder_1_s), .cout(coa), .cin(cia));
  alures alures_1 (.Z(or_1_out[1]), .ares(adder_1_s), .aMSB(A[7]), .bMSB(B[7]), .P(or_1_out[2]), .V(or_1_out[3]));
  _8bitbuffer u_8bitbuffer_1 (.I(adder_1_s), .O(res), .en(en));
  _4bitbuffer u_4bitbuffer_1 (.I(or_1_out), .O({V, P, Z, C}), .en(en));
  and and_2 (and_2_out, not_shift, coa);
  or or_1 (or_1_out[0], and_2_out, and_3_out);
  not not_3 (not_3_out, not_shift);
  and and_3 (and_3_out, not_3_out, cos);
  and and_4 (and_4_out, cos, not_shift);
  or or_2 (cia, Subtract_Function, and_4_out);

  // Other names for the same wires on the sheet: aMSB = A[7]; bMSB = B[7]; enable = en; f0 = fn[0];
  //   lfn[3:0] = fn[3:0]; f1 = fn[1]; f2 = fn[2]; f3 = fn[3]; f4 = fn[4]; sfn[1:0] = fn[5:4]; f5 = fn[5]

  // Notes on the sheet:
  //   The 'NOT B' logic function is used for 'Subtract'
  //   We need to set Carry if this is the case
  //   If we are SHR or SHL we need to ignore carry results from ADDER unit
endmodule

module adder (
  input  [7:0] A,
  input  [7:0] B,
  input  cin,
  output [7:0] S,
  output cout
);

  wire full_adder_1_co, full_adder_2_co, full_adder_3_co, full_adder_4_co, full_adder_5_co, full_adder_6_co,
       full_adder_7_co;

  full_adder full_adder_1 (.A(A[0]), .B(B[0]), .Ci(cin), .S(S[0]), .Co(full_adder_1_co));
  full_adder full_adder_2 (.A(A[1]), .B(B[1]), .Ci(full_adder_1_co), .S(S[1]), .Co(full_adder_2_co));
  full_adder full_adder_3 (.A(A[2]), .B(B[2]), .Ci(full_adder_2_co), .S(S[2]), .Co(full_adder_3_co));
  full_adder full_adder_4 (.A(A[3]), .B(B[3]), .Ci(full_adder_3_co), .S(S[3]), .Co(full_adder_4_co));
  full_adder full_adder_5 (.A(A[4]), .B(B[4]), .Ci(full_adder_4_co), .S(S[4]), .Co(full_adder_5_co));
  full_adder full_adder_6 (.A(A[5]), .B(B[5]), .Ci(full_adder_5_co), .S(S[5]), .Co(full_adder_6_co));
  full_adder full_adder_7 (.A(A[6]), .B(B[6]), .Ci(full_adder_6_co), .S(S[6]), .Co(full_adder_7_co));
  full_adder full_adder_8 (.A(A[7]), .B(B[7]), .Ci(full_adder_7_co), .S(S[7]), .Co(cout));
endmodule

module \logic  (
  input  [7:0] B,
  input  [7:0] A,
  input  [3:0] lfnc,
  output [7:0] Res
);

  wire en;

  Multiplexer #(.select(2)) multiplexer_1 (
    .in0(lfnc[0]), .in1(lfnc[1]), .in2(lfnc[2]), .in3(lfnc[3]), .out(Res[0]), .sel({B[0], A[0]}), .en(en));
  Multiplexer #(.select(2)) multiplexer_2 (
    .in0(lfnc[0]), .in1(lfnc[1]), .in2(lfnc[2]), .in3(lfnc[3]), .out(Res[1]), .sel({B[1], A[1]}), .en(en));
  Multiplexer #(.select(2)) multiplexer_3 (
    .in0(lfnc[0]), .in1(lfnc[1]), .in2(lfnc[2]), .in3(lfnc[3]), .out(Res[2]), .sel({B[2], A[2]}), .en(en));
  Multiplexer #(.select(2)) multiplexer_4 (
    .in0(lfnc[0]), .in1(lfnc[1]), .in2(lfnc[2]), .in3(lfnc[3]), .out(Res[3]), .sel({B[3], A[3]}), .en(en));
  Multiplexer #(.select(2)) multiplexer_5 (
    .in0(lfnc[0]), .in1(lfnc[1]), .in2(lfnc[2]), .in3(lfnc[3]), .out(Res[4]), .sel({B[4], A[4]}), .en(en));
  Multiplexer #(.select(2)) multiplexer_6 (
    .in0(lfnc[0]), .in1(lfnc[1]), .in2(lfnc[2]), .in3(lfnc[3]), .out(Res[5]), .sel({B[5], A[5]}), .en(en));
  Multiplexer #(.select(2)) multiplexer_7 (
    .in0(lfnc[0]), .in1(lfnc[1]), .in2(lfnc[2]), .in3(lfnc[3]), .out(Res[6]), .sel({B[6], A[6]}), .en(en));
  Multiplexer #(.select(2)) multiplexer_8 (
    .in0(lfnc[0]), .in1(lfnc[1]), .in2(lfnc[2]), .in3(lfnc[3]), .out(Res[7]), .sel({B[7], A[7]}), .en(en));

  // Other names for the same wires on the sheet: fnc[3:0] = lfnc; r0 = Res[0]; r1 = Res[1]; r2 = Res[2]; r3 = Res[3];
  //   r4 = Res[4]; r5 = Res[5]; r6 = Res[6]; r7 = Res[7]

  // Notes on the sheet:
  //   LOGIC Units Made out of MUXes
  //   0xa          A
  //   0xc          B
  //   0x8          AND
  //   0xe          OR
  //   0x6          XOR
  //   0x1          NOR
  //   0xf          255
  //   lfnc         Logic Function
  //   0x7          NAND
  //   0x3          NOT B
  //   0x5          NOT A
  //   0x0         Zero (0)
endmodule

module shift (
  input  [7:0] A,
  input  [1:0] sfn,
  input  cin,
  output [7:0] res,
  output cout
);

  wire en;

  Multiplexer #(.select(2)) multiplexer_1 (
    .in0(A[0]), .in1(A[1]), .in2(cin), .in3(1'b0), .out(res[0]), .sel(sfn), .en(en));
  Multiplexer #(.select(2)) multiplexer_2 (
    .in0(A[4]), .in1(A[5]), .in2(A[3]), .in3(1'b0), .out(res[4]), .sel(sfn), .en(en));
  Multiplexer #(.select(2)) multiplexer_3 (
    .in0(A[1]), .in1(A[2]), .in2(A[0]), .in3(1'b0), .out(res[1]), .sel(sfn), .en(en));
  Multiplexer #(.select(2)) multiplexer_4 (
    .in0(A[5]), .in1(A[6]), .in2(A[4]), .in3(1'b0), .out(res[5]), .sel(sfn), .en(en));
  Multiplexer #(.select(2)) multiplexer_5 (
    .in0(cin), .in1(A[0]), .in2(A[7]), .in3(1'b0), .out(cout), .sel(sfn), .en(en));
  Multiplexer #(.select(2)) multiplexer_6 (
    .in0(A[2]), .in1(A[3]), .in2(A[1]), .in3(1'b0), .out(res[2]), .sel(sfn), .en(en));
  Multiplexer #(.select(2)) multiplexer_7 (
    .in0(A[6]), .in1(A[7]), .in2(A[5]), .in3(1'b0), .out(res[6]), .sel(sfn), .en(en));
  Multiplexer #(.select(2)) multiplexer_8 (
    .in0(A[3]), .in1(A[4]), .in2(A[2]), .in3(1'b0), .out(res[3]), .sel(sfn), .en(en));
  Multiplexer #(.select(2)) multiplexer_9 (
    .in0(A[7]), .in1(cin), .in2(A[6]), .in3(1'b0), .out(res[7]), .sel(sfn), .en(en));

  // Other names for the same wires on the sheet: r0 = res[0]; r1 = res[1]; r2 = res[2]; r3 = res[3]; r4 = res[4];
  //   r5 = res[5]; r6 = res[6]; r7 = res[7]; sfnc[1:0] = sfn

  // Notes on the sheet:
  //   sfnc         Shift Function
  //   b00          no change
  //   b01          Shift Right
  //   b10          Shift Left
  //   b11          Clear
endmodule

// fadd
module full_adder (
  input  A,
  input  B,
  input  Ci,
  output S,
  output Co
);

  wire and_1_out, and_2_out, and_3_out, or_1_out, xor_1_out;

  xor xor_1 (xor_1_out, A, B);
  and and_1 (and_1_out, A, B);
  and and_2 (and_2_out, A, Ci);
  and and_3 (and_3_out, B, Ci);
  or or_1 (or_1_out, and_1_out, and_2_out);
  xor xor_2 (S, xor_1_out, Ci);
  or or_2 (Co, or_1_out, and_3_out);

  // Notes on the sheet:
  //   Full 1-bit Adder (carry In, A, B) --> (S(um), carry out)
endmodule

// ALU Res
module alures (
  input  [7:0] ares,
  input  aMSB,
  input  bMSB,
  output Z,
  output P,
  output V
);

  wire or_1_out, or_2_out, or_3_out, or_4_out, or_5_out, or_6_out, xor_1_out, xor_2_out, xor_3_out,
       xor_4_out, xor_5_out, xor_6_out, xor_7_out, xor_8_out;

  xor xor_1 (xor_1_out, aMSB, ares[7]);
  xor xor_2 (xor_2_out, ares[7], bMSB);
  and and_1 (V, xor_1_out, xor_2_out);
  or or_1 (or_1_out, ares[7], ares[6]);
  or or_2 (or_2_out, ares[5], ares[4]);
  or or_3 (or_3_out, ares[3], ares[2]);
  or or_4 (or_4_out, ares[1], ares[0]);
  xor xor_3 (xor_3_out, ares[7], ares[6]);
  xor xor_4 (xor_4_out, ares[5], ares[4]);
  xor xor_5 (xor_5_out, ares[3], ares[2]);
  xor xor_6 (xor_6_out, ares[1], ares[0]);
  or or_5 (or_5_out, or_1_out, or_2_out);
  or or_6 (or_6_out, or_3_out, or_4_out);
  xor xor_7 (xor_7_out, xor_3_out, xor_4_out);
  xor xor_8 (xor_8_out, xor_5_out, xor_6_out);
  nor nor_1 (Z, or_5_out, or_6_out);
  xor xor_9 (P, xor_7_out, xor_8_out);

  // Other names for the same wires on the sheet: r0 = ares[0]; r1 = ares[1]; r2 = ares[2]; r3 = ares[3]; r4 = ares[4];
  //   r5 = ares[5]; r6 = ares[6]; r7 = ares[7]; Overflow = V; ParityOdd = P; Zero = Z
endmodule

module control (
  input  in_1
);

  ROM #(.addrWidth(16)) rom_1 ();  // open: addr, data, sel

  // Notes on the sheet:
  //   contents of rom_1 (hex, n*v repeats v):
  //   0 1 2 3 4 5 6 7 8 9 a b c d e f 10 11 12 13 14 15 16 17 18 19 1a 1b 1c 1d 1e 1f 67*0 ff 65435*0 ff
endmodule

// RING
module ringcounter (
  input  clk,
  input  clr,
  output [5:0] Q
);

  D_Flip_Flop d_ff_1 (.clk(clk), .D(Q[4]), .Q(Q[5]), .reset(clr));  // open: Qn, preset, en
  D_Flip_Flop d_ff_2 (.clk(clk), .D(Q[3]), .Q(Q[4]), .reset(clr));  // open: Qn, preset, en
  D_Flip_Flop d_ff_3 (.clk(clk), .D(Q[2]), .Q(Q[3]), .reset(clr));  // open: Qn, preset, en
  D_Flip_Flop d_ff_4 (.clk(clk), .D(Q[1]), .Q(Q[2]), .reset(clr));  // open: Qn, preset, en
  D_Flip_Flop d_ff_5 (.clk(clk), .D(Q[0]), .Q(Q[1]), .reset(clr));  // open: Qn, preset, en
  D_Flip_Flop d_ff_6 (.clk(clk), .D(Q[5]), .Q(Q[0]), .preset(clr));  // open: Qn, en, reset

  // Notes on the sheet:
  //   clr: pull=down
endmodule

module pulse (
  input  clk,
  input  req,
  output warm,
  output cold
);

  wire COLDPULSE, d_ff_1_q, d_ff_2_q, d_ff_2_qn, d_ff_3_q;

  D_Flip_Flop d_ff_1 (.clk(clk), .D(req), .Q(d_ff_1_q));  // open: Qn, preset, en, reset
  D_Flip_Flop d_ff_2 (.clk(clk), .D(d_ff_1_q), .Q(d_ff_2_q), .Qn(d_ff_2_qn));  // open: preset, en, reset
  D_Flip_Flop d_ff_3 (.clk(clk), .D(d_ff_2_qn), .Q(d_ff_3_q));  // open: Qn, preset, en, reset
  and and_1 (cold, d_ff_2_q, d_ff_3_q);
  not not_1 (COLDPULSE, d_ff_3_q);

  assign warm = cold;

  // Other names for the same wires on the sheet: request = req; WARMPULSE = cold
endmodule

// _8buffer
module _8bitbuffer (
  input  [7:0] I,
  input  en,
  output [7:0] O
);

  _4bitbuffer u_4bitbuffer_1 (.I(I[7:4]), .O(O[7:4]), .en(en));
  _4bitbuffer u_4bitbuffer_2 (.I(I[3:0]), .O(O[3:0]), .en(en));

  // Other names for the same wires on the sheet: Lin[3:0] = I[3:0]; Hin[3:0] = I[7:4]; Lout[3:0] = O[3:0];
  //   Hout[3:0] = O[7:4]
endmodule

module _4bitbuffer (
  input  [3:0] I,
  input  en,
  output [3:0] O
);

  assign O[0] = en ? I[0] : 1'bz;  // Controlled_Buffer controlled_buffer_1
  assign O[1] = en ? I[1] : 1'bz;  // Controlled_Buffer controlled_buffer_2
  assign O[2] = en ? I[2] : 1'bz;  // Controlled_Buffer controlled_buffer_3
  assign O[3] = en ? I[3] : 1'bz;  // Controlled_Buffer controlled_buffer_4
endmodule

module decimaldisplay (
  input  clk,
  input  [3:0] digit,
  input  reset
);

  wire clock_1_out;

  Clock clock_1 (.out(clock_1_out));
  displaycounter displaycounter_1 (.clk(clock_1_out), .clr(reset), .Q(digit));
endmodule

// 4 ring
module displaycounter (
  input  clk,
  input  clr,
  output [3:0] Q
);

  D_Flip_Flop d_ff_1 (.clk(clk), .D(Q[2]), .Q(Q[3]), .reset(clr));  // open: Qn, preset, en
  D_Flip_Flop d_ff_2 (.clk(clk), .D(Q[1]), .Q(Q[2]), .reset(clr));  // open: Qn, preset, en
  D_Flip_Flop d_ff_3 (.clk(clk), .D(Q[0]), .Q(Q[1]), .reset(clr));  // open: Qn, preset, en
  D_Flip_Flop d_ff_4 (.clk(clk), .D(Q[3]), .Q(Q[0]), .preset(clr));  // open: Qn, en, reset

  // Notes on the sheet:
  //   clr: pull=up
endmodule
