// Logisim project newcpu.circ as structural Verilog: 25 circuits, main circuit main
// RESET
module main (
  input  [15:0] in_1,
  input  [15:0] in_2,
  input  [3:0] in_3,
  input  [2:0] in_4,
  input  [1:0] in_5,
  input  [5:0] in_6,
  input  [3:0] in_7,
  input  [7:0] in_8,
  output [5:0] out_9,
  output [15:0] out_10,
  output [15:0] out_11,
  output [7:0] out_12
);

  wire and_1_out, and_2_out, and_3_out, and_4_out, and_5_out, and_6_out, and_7_out, and_8_out, button_1_out,
       button_2_out, button_3_out, button_4_out, button_5_out, clCLOCKPC, clDISP, clDISPLATCH, clEN4REG,
       clEnAH8BUS, clEnAL8BUS, clENCons, clEnMAREG, clENRAM, clENREGA, clENREGB, clENREGF, clENREGR,
       clEnSPREG, CLK, clNotEnPCREG, clPCcount, clSelBank0, clSelBank1, clSelConst0, clSelConst1,
       clSelConst2, clWAH8BUS, clWAL8BUS, clWMAREG, clWPCREG, clWREGA, clWREGB, clWREGB0, clWREGB1, clWREGB2,
       clWREGB3, clWREGF, clWREGI, clWREGO, clWREGR, clWSPREG, cpuCLK, cpuCLKdiv2, d1, d2, d3, d4, flagC,
       flagP, hex7seg_1_a, hex7seg_1_b, hex7seg_1_c, hex7seg_1_d, hex7seg_1_dp, hex7seg_1_e, hex7seg_1_f,
       hex7seg_1_g, hex7seg_2_a, hex7seg_2_b, hex7seg_2_c, hex7seg_2_d, hex7seg_2_dp, hex7seg_2_e,
       hex7seg_2_f, hex7seg_2_g, hex7seg_3_a, hex7seg_3_b, hex7seg_3_c, hex7seg_3_d, hex7seg_3_dp,
       hex7seg_3_e, hex7seg_3_f, hex7seg_3_g, hex7seg_4_a, hex7seg_4_b, hex7seg_4_c, hex7seg_4_d,
       hex7seg_4_dp, hex7seg_4_e, hex7seg_4_f, hex7seg_4_g, hex7seg_5_a, hex7seg_5_b, hex7seg_5_c,
       hex7seg_5_d, hex7seg_5_dp, hex7seg_5_e, hex7seg_5_f, hex7seg_5_g, hex7seg_6_a, hex7seg_6_b,
       hex7seg_6_c, hex7seg_6_d, hex7seg_6_dp, hex7seg_6_e, hex7seg_6_f, hex7seg_6_g, hex7seg_7_a,
       hex7seg_7_b, hex7seg_7_c, hex7seg_7_d, hex7seg_7_dp, hex7seg_7_e, hex7seg_7_f, hex7seg_7_g,
       hex7seg_8_a, hex7seg_8_b, hex7seg_8_c, hex7seg_8_d, hex7seg_8_dp, hex7seg_8_e, hex7seg_8_f,
       hex7seg_8_g, hex7seg_9_a, hex7seg_9_b, hex7seg_9_c, hex7seg_9_d, hex7seg_9_dp, hex7seg_9_e,
       hex7seg_9_f, hex7seg_9_g, hex7seg_10_a, hex7seg_10_b, hex7seg_10_c, hex7seg_10_d, hex7seg_10_dp,
       hex7seg_10_e, hex7seg_10_f, hex7seg_10_g, hex7seg_11_a, hex7seg_11_b, hex7seg_11_c, hex7seg_11_d,
       hex7seg_11_dp, hex7seg_11_e, hex7seg_11_f, hex7seg_11_g, hex7seg_12_a, hex7seg_12_b, hex7seg_12_c,
       hex7seg_12_d, hex7seg_12_dp, hex7seg_12_e, hex7seg_12_f, hex7seg_12_g, hex7seg_13_a, hex7seg_13_b,
       hex7seg_13_c, hex7seg_13_d, hex7seg_13_dp, hex7seg_13_e, hex7seg_13_f, hex7seg_13_g, hex7seg_14_a,
       hex7seg_14_b, hex7seg_14_c, hex7seg_14_d, hex7seg_14_dp, hex7seg_14_e, hex7seg_14_f, hex7seg_14_g,
       hex7seg_15_a, hex7seg_15_b, hex7seg_15_c, hex7seg_15_d, hex7seg_15_dp, hex7seg_15_e, hex7seg_15_f,
       hex7seg_15_g, hex7seg_16_a, hex7seg_16_b, hex7seg_16_c, hex7seg_16_d, hex7seg_16_dp, hex7seg_16_e,
       hex7seg_16_f, hex7seg_16_g, nCLK, ncpuCLK, pause, pull_resistor_3_node, pull_resistor_7_node,
       pull_resistor_8_node, pull_resistor_13_node, pull_resistor_14_node, pull_resistor_15_node,
       pull_resistor_16_node, uRESET;
  wire [3:0] FLAGBUS, s1h, s1l, s2h, s2l, s3h, s3l, s4h, s4l;
  wire [4:0] counter_1_q;
  wire [5:0] ConRing;
  wire [6:3] rom_2_data;
  wire [7:0] ABUSHreg_q, ABUSLreg_q, ALURBUS, AREGBUS, BREGBUS, IREGBUS, OREGBUS, RREGBUS,
       segdecdisplay_1_hseg;
  wire [7:1] FLAGS;
  wire [9:0] controller_1_addr;
  wire [11:0] CON;
  wire [15:0] A16BUS, MARBUS, PCVALUE, SPBUS;

  Button button_1 (.out(button_1_out));
  Button button_2 (.out(button_2_out));
  hex7seg hex7seg_1 (
    .a(hex7seg_1_a), .b(hex7seg_1_b), .c(hex7seg_1_c), .d(hex7seg_1_d), .e(hex7seg_1_e), .f(hex7seg_1_f),
    .g(hex7seg_1_g), .dp(hex7seg_1_dp), .en(pull_resistor_7_node), .value(PCVALUE[15:12]));  // open: dot
  hex7seg hex7seg_2 (
    .a(hex7seg_2_a), .b(hex7seg_2_b), .c(hex7seg_2_c), .d(hex7seg_2_d), .e(hex7seg_2_e), .f(hex7seg_2_f),
    .g(hex7seg_2_g), .dp(hex7seg_2_dp), .en(pull_resistor_8_node), .value(SPBUS[15:12]));  // open: dot
  Button button_3 (.out(button_3_out));
  Button button_4 (.out(button_4_out));
  Register Areg (.D(out_12), .en(clWREGA), .clk(cpuCLK), .Q(AREGBUS), .clr(uRESET));
  Register Rreg (.D(ALURBUS), .en(clWREGR), .clk(cpuCLK), .Q(RREGBUS), .clr(uRESET));
  _7_Segment_Display u_7_segment_display_1 (
    .g(hex7seg_1_g), .f(hex7seg_1_f), .a(hex7seg_1_a), .b(hex7seg_1_b), .e(hex7seg_1_e), .d(hex7seg_1_d),
    .c(hex7seg_1_c), .dp(hex7seg_1_dp));
  hex7seg hex7seg_3 (
    .a(hex7seg_3_a), .b(hex7seg_3_b), .c(hex7seg_3_c), .d(hex7seg_3_d), .e(hex7seg_3_e), .f(hex7seg_3_f),
    .g(hex7seg_3_g), .dp(hex7seg_3_dp), .en(pull_resistor_7_node), .value(PCVALUE[11:8]));  // open: dot
  _7_Segment_Display u_7_segment_display_2 (
    .g(hex7seg_2_g), .f(hex7seg_2_f), .a(hex7seg_2_a), .b(hex7seg_2_b), .e(hex7seg_2_e), .d(hex7seg_2_d),
    .c(hex7seg_2_c), .dp(hex7seg_2_dp));
  hex7seg hex7seg_4 (
    .a(hex7seg_4_a), .b(hex7seg_4_b), .c(hex7seg_4_c), .d(hex7seg_4_d), .e(hex7seg_4_e), .f(hex7seg_4_f),
    .g(hex7seg_4_g), .dp(hex7seg_4_dp), .en(pull_resistor_8_node), .value(SPBUS[11:8]));  // open: dot
  cpuclock cpuclock_1 (.clk(CLK), .clk2(cpuCLKdiv2), .cpuclk(cpuCLK), .pause(pause), .step(button_3_out));
  toggleswitch toggleswitch_1 (.switch(pause), .clk(CLK), .res(uRESET), .I(button_4_out));  // open: latch
  debounce debounce_1 (.resp(clWREGO), .req(button_1_out), .clk(CLK));
  debounce debounce_2 (.resp(uRESET), .req(button_2_out), .clk(CLK));
  Register ABUSLreg (.D(out_12), .en(clWAL8BUS), .clk(cpuCLK), .Q(ABUSLreg_q), .clr(uRESET));
  Register ABUSHreg (.D(out_12), .en(clWAH8BUS), .clk(cpuCLK), .Q(ABUSHreg_q), .clr(uRESET));
  assign out_12 = clENREGA ? AREGBUS : 8'bz;  // Controlled_Buffer controlled_buffer_1
  Pull_Resistor pull_resistor_1 (.node(clENREGA));
  assign out_12 = clENREGR ? RREGBUS : 8'bz;  // Controlled_Buffer controlled_buffer_2
  Pull_Resistor pull_resistor_2 (.node(clENREGR));
  constantbank constantbank_1 (.Q(out_12), .regsel({clSelConst2, clSelConst1, clSelConst0}), .en(clENCons));
  // Probe on AREGBUS
  Pull_Resistor pull_resistor_3 (.node(pull_resistor_3_node));
  _7_Segment_Display u_7_segment_display_3 (
    .g(hex7seg_3_g), .f(hex7seg_3_f), .a(hex7seg_3_a), .b(hex7seg_3_b), .e(hex7seg_3_e), .d(hex7seg_3_d),
    .c(hex7seg_3_c), .dp(hex7seg_3_dp));
  _7_Segment_Display u_7_segment_display_4 (
    .g(hex7seg_4_g), .f(hex7seg_4_f), .a(hex7seg_4_a), .b(hex7seg_4_b), .e(hex7seg_4_e), .d(hex7seg_4_d),
    .c(hex7seg_4_c), .dp(hex7seg_4_dp));
  not not_1 (nCLK, CLK);
  not not_2 (ncpuCLK, cpuCLK);
  LED led_1 (.in(clWREGO));
  LED led_2 (.in(uRESET));
  assign out_10[7:0] = clEnAL8BUS ? ABUSLreg_q : 8'bz;  // Controlled_Buffer controlled_buffer_3
  Pull_Resistor pull_resistor_4 (.node(clEnAL8BUS));
  assign out_10[15:8] = clEnAH8BUS ? ABUSHreg_q : 8'bz;  // Controlled_Buffer controlled_buffer_4
  Pull_Resistor pull_resistor_5 (.node(clEnAH8BUS));
  _7_Segment_Display u_7_segment_display_5 (
    .g(hex7seg_5_g), .f(hex7seg_5_f), .a(hex7seg_5_a), .b(hex7seg_5_b), .e(hex7seg_5_e), .d(hex7seg_5_d),
    .c(hex7seg_5_c), .dp(hex7seg_5_dp));
  hex7seg hex7seg_5 (
    .a(hex7seg_5_a), .b(hex7seg_5_b), .c(hex7seg_5_c), .d(hex7seg_5_d), .e(hex7seg_5_e), .f(hex7seg_5_f),
    .g(hex7seg_5_g), .dp(hex7seg_5_dp), .en(pull_resistor_7_node), .value(PCVALUE[7:4]));  // open: dot
  _7_Segment_Display u_7_segment_display_6 (
    .g(hex7seg_6_g), .f(hex7seg_6_f), .a(hex7seg_6_a), .b(hex7seg_6_b), .e(hex7seg_6_e), .d(hex7seg_6_d),
    .c(hex7seg_6_c), .dp(hex7seg_6_dp));
  hex7seg hex7seg_6 (
    .a(hex7seg_6_a), .b(hex7seg_6_b), .c(hex7seg_6_c), .d(hex7seg_6_d), .e(hex7seg_6_e), .f(hex7seg_6_f),
    .g(hex7seg_6_g), .dp(hex7seg_6_dp), .en(pull_resistor_8_node), .value(SPBUS[7:4]));  // open: dot
  LED led_3 (.in(pause));
  Register Breg (.D(out_12), .en(clWREGB), .clk(cpuCLK), .Q(BREGBUS), .clr(uRESET));
  Register Freg (
    .D({4'b0000, FLAGBUS}), .en(clWREGF), .clk(cpuCLK), .Q({FLAGS[7:3], flagP, FLAGS[1], flagC}), .clr(uRESET));
  assign out_12 = clENREGF ? {FLAGS[7:3], flagP, FLAGS[1], flagC} : 8'bz;  // Controlled_Buffer controlled_buffer_5
  Pull_Resistor pull_resistor_6 (.node(clENREGF));
  // Probe on out_12
  rammodule rammodule_1 (
    .dout(out_12), .addr(out_10), .clk(cpuCLK), .din(out_12), .oe(clENRAM), .we(pull_resistor_3_node));
  _7_Segment_Display u_7_segment_display_7 (
    .g(hex7seg_7_g), .f(hex7seg_7_f), .a(hex7seg_7_a), .b(hex7seg_7_b), .e(hex7seg_7_e), .d(hex7seg_7_d),
    .c(hex7seg_7_c), .dp(hex7seg_7_dp));
  hex7seg hex7seg_7 (
    .a(hex7seg_7_a), .b(hex7seg_7_b), .c(hex7seg_7_c), .d(hex7seg_7_d), .e(hex7seg_7_e), .f(hex7seg_7_f),
    .g(hex7seg_7_g), .dp(hex7seg_7_dp), .en(pull_resistor_7_node), .value(PCVALUE[3:0]));  // open: dot
  _7_Segment_Display u_7_segment_display_8 (
    .g(hex7seg_8_g), .f(hex7seg_8_f), .a(hex7seg_8_a), .b(hex7seg_8_b), .e(hex7seg_8_e), .d(hex7seg_8_d),
    .c(hex7seg_8_c), .dp(hex7seg_8_dp));
  hex7seg hex7seg_8 (
    .a(hex7seg_8_a), .b(hex7seg_8_b), .c(hex7seg_8_c), .d(hex7seg_8_d), .e(hex7seg_8_e), .f(hex7seg_8_f),
    .g(hex7seg_8_g), .dp(hex7seg_8_dp), .en(pull_resistor_8_node), .value(SPBUS[3:0]));  // open: dot
  ring6 ring6_1 (.Q(out_9), .clr(uRESET), .clk(CLK));
  Counter #(.max('h1f), .width(5)) counter_1 (.clk(cpuCLK), .Q(counter_1_q));  // open: clr, load, up, count, D, carry
  Pull_Resistor #(.pull(1)) pull_resistor_7 (.node(pull_resistor_7_node));
  Pull_Resistor #(.pull(1)) pull_resistor_8 (.node(pull_resistor_8_node));
  Register #(.width(16)) SPReg (.D(A16BUS), .en(clWSPREG), .clk(cpuCLK), .Q(SPBUS), .clr(uRESET));
  Register #(.width(16)) MAReg (.D(A16BUS), .en(clWMAREG), .clk(cpuCLK), .Q(MARBUS), .clr(uRESET));
  // Probe on out_12
  assign out_12 = clENREGB ? BREGBUS : 8'bz;  // Controlled_Buffer controlled_buffer_6
  Pull_Resistor pull_resistor_9 (.node(clENREGB));
  // Probe on {FLAGS[7:3], flagP, FLAGS[1], flagC}
  // Probe on ConRing
  controller controller_1 (.clr(uRESET), .opcode(in_7), .Q(ConRing), .addr(controller_1_addr), .cntrl(CON));
  // Probe on CON
  hex7seg hex7seg_9 (
    .a(hex7seg_9_a), .b(hex7seg_9_b), .c(hex7seg_9_c), .d(hex7seg_9_d), .e(hex7seg_9_e), .f(hex7seg_9_f),
    .g(hex7seg_9_g), .dp(hex7seg_9_dp), .en(pull_resistor_13_node), .value(AREGBUS[7:4]));  // open: dot
  hex7seg hex7seg_10 (
    .a(hex7seg_10_a), .b(hex7seg_10_b), .c(hex7seg_10_c), .d(hex7seg_10_d), .e(hex7seg_10_e),
    .f(hex7seg_10_f), .g(hex7seg_10_g), .dp(hex7seg_10_dp), .en(pull_resistor_14_node), .value(BREGBUS[7:4]));  // open: dot
  and and_1 (and_1_out, ~1'b0, ~1'b0, 1'b1, 1'b1, ~1'b0, ~1'b0);  // AND_Gate
  LED led_4 (.in(and_1_out));
  assign A16BUS = clEnSPREG ? SPBUS : 16'bz;  // Controlled_Buffer controlled_buffer_7
  Pull_Resistor pull_resistor_10 (.node(clEnSPREG));
  assign A16BUS = clEnMAREG ? MARBUS : 16'bz;  // Controlled_Buffer controlled_buffer_8
  Pull_Resistor pull_resistor_11 (.node(clEnMAREG));
  // Digital_Oscilloscope digital_oscilloscope_1: pin names not known; wires that end beside it: cpuCLK, ConRing[0], ConRing[1], ConRing[2]
  _7_Segment_Display u_7_segment_display_9 (
    .g(hex7seg_9_g), .f(hex7seg_9_f), .a(hex7seg_9_a), .b(hex7seg_9_b), .e(hex7seg_9_e), .d(hex7seg_9_d),
    .c(hex7seg_9_c), .dp(hex7seg_9_dp));
  _7_Segment_Display u_7_segment_display_10 (
    .g(hex7seg_10_g), .f(hex7seg_10_f), .a(hex7seg_10_a), .b(hex7seg_10_b), .e(hex7seg_10_e),
    .d(hex7seg_10_d), .c(hex7seg_10_c), .dp(hex7seg_10_dp));
  and and_2 (and_2_out, ~1'b0, ~1'b0, ~1'b1, ~1'b1, 1'b0, 1'b0);  // AND_Gate
  LED led_5 (.in(and_2_out));
  Button button_5 (.out(button_5_out));
  Pull_Resistor pull_resistor_12 ();  // open: node
  Register IReg (.D(out_12), .en(clWREGI), .clk(cpuCLK), .Q(IREGBUS), .clr(uRESET));
  ROM #(.addrWidth(5)) rom_1 (
    .addr(counter_1_q),
    .data({clWREGO, clWREGR, clWREGB, clWREGA, clSelConst2, clSelConst1, clSelConst0, clENCons}));
  ROM #(.addrWidth(5)) rom_2 (
    .addr(counter_1_q),
    .data({clCLOCKPC, rom_2_data[6], clWREGI, rom_2_data[4:3], clENREGA, clENREGB, clENREGR}));
  _7_Segment_Display u_7_segment_display_11 (
    .g(hex7seg_11_g), .f(hex7seg_11_f), .a(hex7seg_11_a), .b(hex7seg_11_b), .e(hex7seg_11_e),
    .d(hex7seg_11_d), .c(hex7seg_11_c), .dp(hex7seg_11_dp));
  hex7seg hex7seg_11 (
    .a(hex7seg_11_a), .b(hex7seg_11_b), .c(hex7seg_11_c), .d(hex7seg_11_d), .e(hex7seg_11_e),
    .f(hex7seg_11_f), .g(hex7seg_11_g), .dp(hex7seg_11_dp), .en(pull_resistor_13_node), .value(AREGBUS[3:0]));  // open: dot
  _7_Segment_Display u_7_segment_display_12 (
    .g(hex7seg_12_g), .f(hex7seg_12_f), .a(hex7seg_12_a), .b(hex7seg_12_b), .e(hex7seg_12_e),
    .d(hex7seg_12_d), .c(hex7seg_12_c), .dp(hex7seg_12_dp));
  hex7seg hex7seg_12 (
    .a(hex7seg_12_a), .b(hex7seg_12_b), .c(hex7seg_12_c), .d(hex7seg_12_d), .e(hex7seg_12_e),
    .f(hex7seg_12_f), .g(hex7seg_12_g), .dp(hex7seg_12_dp), .en(pull_resistor_14_node), .value(BREGBUS[3:0]));  // open: dot
  and and_3 (and_3_out, 1'b0, ~1'b0, ~1'b1, ~1'b1, ~1'b0, ~1'b0);  // AND_Gate
  LED led_6 (.in(and_3_out));
  Button button_6 (.out(clWPCREG));
  // Probe on 6'b001100
  // Probe on controller_1_addr
  hex7seg hex7seg_13 (
    .a(hex7seg_13_a), .b(hex7seg_13_b), .c(hex7seg_13_c), .d(hex7seg_13_d), .e(hex7seg_13_e),
    .f(hex7seg_13_f), .g(hex7seg_13_g), .dp(hex7seg_13_dp), .en(pull_resistor_15_node), .value(IREGBUS[7:4]));  // open: dot
  Pull_Resistor #(.pull(1)) pull_resistor_13 (.node(pull_resistor_13_node));
  hex7seg hex7seg_14 (
    .a(hex7seg_14_a), .b(hex7seg_14_b), .c(hex7seg_14_c), .d(hex7seg_14_d), .e(hex7seg_14_e),
    .f(hex7seg_14_f), .g(hex7seg_14_g), .dp(hex7seg_14_dp), .en(pull_resistor_16_node), .value(OREGBUS[7:4]));  // open: dot
  Pull_Resistor #(.pull(1)) pull_resistor_14 (.node(pull_resistor_14_node));
  and and_4 (and_4_out, ~1'b0, 1'b0, ~1'b1, ~1'b1, ~1'b0, ~1'b0);  // AND_Gate
  LED led_7 (.in(and_4_out));
  LED led_8 (.in(clDISP));
  toggleswitch toggleswitch_2 (.switch(clDISP), .latch(clDISPLATCH), .clk(CLK), .res(uRESET), .I(button_5_out));
  // Probe on out_12
  alu alu_1 (
    .res(ALURBUS), .C(FLAGBUS[0]), .Z(FLAGBUS[1]), .P(FLAGBUS[2]), .V(FLAGBUS[3]), .A(AREGBUS), .B(BREGBUS),
    .fn(6'b001100), .cin(flagC), .en(1'b1));
  _7_Segment_Display u_7_segment_display_13 (
    .g(hex7seg_13_g), .f(hex7seg_13_f), .a(hex7seg_13_a), .b(hex7seg_13_b), .e(hex7seg_13_e),
    .d(hex7seg_13_d), .c(hex7seg_13_c), .dp(hex7seg_13_dp));
  hex7seg hex7seg_15 (
    .a(hex7seg_15_a), .b(hex7seg_15_b), .c(hex7seg_15_c), .d(hex7seg_15_d), .e(hex7seg_15_e),
    .f(hex7seg_15_f), .g(hex7seg_15_g), .dp(hex7seg_15_dp), .en(pull_resistor_15_node), .value(IREGBUS[3:0]));  // open: dot
  _7_Segment_Display u_7_segment_display_14 (
    .g(hex7seg_14_g), .f(hex7seg_14_f), .a(hex7seg_14_a), .b(hex7seg_14_b), .e(hex7seg_14_e),
    .d(hex7seg_14_d), .c(hex7seg_14_c), .dp(hex7seg_14_dp));
  and and_5 (and_5_out, 1'b0, 1'b0, 1'b1, ~1'b1, ~1'b0, ~1'b0);  // AND_Gate
  LED led_9 (.in(and_5_out));
  Button button_7 (.out(clWPCREG));
  pcreg pcreg_1 (
    .Dout(out_11), .Din(in_2), .counten(clPCcount), .reset(uRESET), .load(clWPCREG), .clk(ncpuCLK),
    .pcout(clNotEnPCREG));  // open: dbg
  _7_Segment_Display u_7_segment_display_15 (
    .g(hex7seg_15_g), .f(hex7seg_15_f), .a(hex7seg_15_a), .b(hex7seg_15_b), .e(hex7seg_15_e),
    .d(hex7seg_15_d), .c(hex7seg_15_c), .dp(hex7seg_15_dp));
  Pull_Resistor #(.pull(1)) pull_resistor_15 (.node(pull_resistor_15_node));
  _7_Segment_Display u_7_segment_display_16 (
    .g(hex7seg_16_g), .f(hex7seg_16_f), .a(hex7seg_16_a), .b(hex7seg_16_b), .e(hex7seg_16_e),
    .d(hex7seg_16_d), .c(hex7seg_16_c), .dp(hex7seg_16_dp));
  hex7seg hex7seg_16 (
    .a(hex7seg_16_a), .b(hex7seg_16_b), .c(hex7seg_16_c), .d(hex7seg_16_d), .e(hex7seg_16_e),
    .f(hex7seg_16_f), .g(hex7seg_16_g), .dp(hex7seg_16_dp), .en(pull_resistor_16_node), .value(OREGBUS[3:0]));  // open: dot
  and and_6 (and_6_out, 1'b0, 1'b0, 1'b1, 1'b1, 1'b0, ~1'b0);  // AND_Gate
  LED led_10 (.in(and_6_out));
  Register OReg (.D(out_12), .en(clWREGO), .clk(cpuCLK), .Q(OREGBUS), .clr(uRESET));
  reg4bank reg4bank_1 (
    .Q(out_12), .res(uRESET), .en(clEN4REG), .regsel({clSelBank1, clSelBank0}), .clk(cpuCLK),
    .weMask({clWREGB3, clWREGB2, clWREGB1, clWREGB0}), .I(out_12));
  assign out_12 = 1'b0 ? ALURBUS : 8'bz;  // Controlled_Buffer controlled_buffer_9
  LED led_11 (.in(FLAGBUS[0]));
  LED led_12 (.in(FLAGBUS[1]));
  LED led_13 (.in(FLAGBUS[2]));
  LED led_14 (.in(FLAGBUS[3]));
  Pull_Resistor #(.pull(1)) pull_resistor_16 (.node(pull_resistor_16_node));
  and and_7 (and_7_out, 1'b0, 1'b0, ~1'b1, 1'b1, 1'b0, ~1'b0);  // AND_Gate
  LED led_15 (.in(and_7_out));
  // Probe on out_12
  D_Flip_Flop d_ff_1 (.D(clDISP), .clk(clDISPLATCH), .reset(uRESET));  // open: Q, Qn, preset
  _7_Segment_Display digit4 (
    .g(s4h[3]), .f(s4h[2]), .a(s4h[1]), .b(s4h[0]), .e(s4l[3]), .d(s4l[2]), .c(s4l[1]), .dp(s4l[0]));
  // Probe on 6'b001100
  and and_8 (and_8_out, ~1'b0, ~1'b0, ~1'b1, ~1'b1, ~1'b0, ~1'b0);  // AND_Gate
  LED led_16 (.in(and_8_out));
  pcreg4 pcreg4_1 (
    .Dout(out_10), .dbg(PCVALUE), .pcout(clNotEnPCREG), .Din(in_1), .reset(uRESET), .clk(ncpuCLK),
    .load(clWPCREG), .counten(clPCcount));
  _7_Segment_Display digit3 (
    .g(s3h[3]), .f(s3h[2]), .a(s3h[1]), .b(s3h[0]), .e(s3l[3]), .d(s3l[2]), .c(s3l[1]), .dp(s3l[0]));
  _7_Segment_Display digit2 (
    .g(s2h[3]), .f(s2h[2]), .a(s2h[1]), .b(s2h[0]), .e(s2l[3]), .d(s2l[2]), .c(s2l[1]), .dp(s2l[0]));
  _7_Segment_Display digit1 (
    .g(s1h[3]), .f(s1h[2]), .a(s1h[1]), .b(s1h[0]), .e(s1l[3]), .d(s1l[2]), .c(s1l[1]), .dp(s1l[0]));
  // Probe on {d4, d3, d2, d1}
  segdecdisplay segdecdisplay_1 (
    .reset(uRESET), .clk(CLK), .value(OREGBUS), .sign(1'b0), .en(1'b1), .anode({d4, d3, d2, d1}),
    .hseg(segdecdisplay_1_hseg));
  assign {s1h, s1l} = d1 ? segdecdisplay_1_hseg : 8'bz;  // Controlled_Buffer controlled_buffer_10
  assign {s2h, s2l} = d2 ? segdecdisplay_1_hseg : 8'bz;  // Controlled_Buffer controlled_buffer_11
  assign {s3h, s3l} = d3 ? segdecdisplay_1_hseg : 8'bz;  // Controlled_Buffer controlled_buffer_12
  assign {s4h, s4l} = d4 ? segdecdisplay_1_hseg : 8'bz;  // Controlled_Buffer controlled_buffer_13

  // Other names for the same wires on the sheet: ABUS16[15:0] = out_10; AL8BUS[7:0] = out_10[7:0];
  //   AH8BUS[7:0] = out_10[15:8]; T1 = ConRing[0]; T2 = ConRing[1]; T3 = ConRing[2]; T4 = ConRing[3]; T5 = ConRing[4];
  //   T6 = ConRing[5]; DBUS[7:0] = out_12; FLAGS (some bits) = {flagP, flagC}; flagZ = FLAGS[1]; flagV = FLAGS[3];
  //   flu0 = FLAGS[4]; flu1 = FLAGS[5]; flu2 = FLAGS[6]; flu3 = FLAGS[7]; OPERAND[3:0] = IREGBUS[3:0];
  //   OPCODE[3:0] = IREGBUS[7:4]; PROBEA[7:0] = AREGBUS

  // Notes on the sheet:
  //   PC REGISTER
  //   SP REGISTER
  //   16 bit Support for transferring from 8-bit DBUS to ABUS
  //   NOT YET DECIDED IF A or B CAN BE READ BACK
  //   ADD
  //   A REGISTER
  //   B  REGISTER
  //   SUB
  //   contents of rom_1 (hex, n*v repeats v):
  //   0 13 25 40
  //   contents of rom_2 (hex, n*v repeats v):
  //   80
  //   SHIFT LEFT
  //   ALU FUNCTION
  //   SHIFT RIGHT
  //   Instruction  REGISTER
  //   OUTPUT REGISTER (HEX)
  //   AND
  //   OR
  //   PC 16-BIT
  //   DEBUG ONLY
  //   OUTPUT REGISTER
  //   XOR
  //   PC 4-BIT COUNTER (16BIT OUTPUT)
  //   NOP
  //   DEBUG ONLY
  //   OUTPUT REGISTER (DECIMAL)
endmodule

module controller (
  input  clr,
  input  [3:0] opcode,
  output [5:0] Q,
  output [9:0] addr,
  output [11:0] cntrl
);

  wire CLK, cpuCLK, cpuCLKdiv2, nCLK, ncpuCLK, not_3_out, undriven, undriven_2;

  cpuclock cpuclock_1 (.clk(CLK), .clk2(cpuCLKdiv2), .cpuclk(cpuCLK), .pause(undriven_2), .step(undriven));
  ROM #(.addrWidth(10), .dataWidth(12)) rom_1 (.addr({3'b000, opcode, addr[2:0]}), .data(cntrl));
  assign addr[2:0] = Q[0] ? 3'b000 : 3'bz;  // Controlled_Buffer controlled_buffer_1
  assign addr[2:0] = Q[1] ? 3'b001 : 3'bz;  // Controlled_Buffer controlled_buffer_2
  assign addr[2:0] = Q[2] ? 3'b010 : 3'bz;  // Controlled_Buffer controlled_buffer_3
  assign addr[2:0] = Q[3] ? 3'b011 : 3'bz;  // Controlled_Buffer controlled_buffer_4
  assign addr[2:0] = Q[4] ? 3'b100 : 3'bz;  // Controlled_Buffer controlled_buffer_5
  assign addr[2:0] = Q[5] ? 3'b101 : 3'bz;  // Controlled_Buffer controlled_buffer_6
  not not_1 (nCLK, CLK);
  not not_2 (ncpuCLK, cpuCLK);
  not not_3 (not_3_out, cpuCLK);
  ring6 ring6_1 (.Q(Q), .clr(clr), .clk(not_3_out));

  assign addr[9:3] = {3'b000, opcode};

  // Other names for the same wires on the sheet: Qd[2:0] = addr[2:0]; control[11:0] = cntrl

  // Notes on the sheet:
  //   Qd is Log2(Q) * 1
  //   contents of rom_1 (hex, n*v repeats v):
  //   123 456 789 abc def fed 0 0 888 999 aaa bbb ccc ddd
endmodule

module ring4 (
  input  clr,
  input  clk,
  output [3:0] Q
);

  wire q4, q5, q6, q7;

  D_Flip_Flop d_ff_1 (.D(q6), .clk(clk), .Q(q7), .reset(clr));  // open: Qn, preset
  D_Flip_Flop d_ff_2 (.D(q5), .clk(clk), .Q(q6), .reset(clr));  // open: Qn, preset
  D_Flip_Flop d_ff_3 (.D(q4), .clk(clk), .Q(q5), .reset(clr));  // open: Qn, preset
  D_Flip_Flop d_ff_4 (.D(Q[3]), .clk(clk), .Q(q4), .reset(clr));  // open: Qn, preset
  D_Flip_Flop d_ff_5 (.D(Q[2]), .clk(clk), .Q(Q[3]), .reset(clr));  // open: Qn, preset
  D_Flip_Flop d_ff_6 (.D(Q[1]), .clk(clk), .Q(Q[2]), .reset(clr));  // open: Qn, preset
  D_Flip_Flop d_ff_7 (.D(Q[0]), .clk(clk), .Q(Q[1]), .reset(clr));  // open: Qn, preset
  D_Flip_Flop d_ff_8 (.D(Q[3]), .clk(clk), .Q(Q[0]), .preset(clr));  // open: Qn, reset
endmodule

module cpuclock (
  input  pause,
  input  step,
  output clk,
  output cpuclk,
  output clk2
);

  wire and_1_out, and_2_out, d_ff_1_qn, not_1_out;

  Clock clock_1 (.out(clk));
  D_Flip_Flop d_ff_1 (.D(d_ff_1_qn), .clk(clk), .Q(clk2), .Qn(d_ff_1_qn));  // open: preset, reset
  not not_1 (not_1_out, pause);
  and and_1 (and_1_out, clk, not_1_out);
  and and_2 (and_2_out, pause, step);
  or or_1 (cpuclk, and_1_out, and_2_out);

  // Other names for the same wires on the sheet: cpuCLKdiv2 = clk2; MAINCLK = clk
endmodule

module segdecdisplay (
  input  reset,
  input  clk,
  input  [7:0] value,
  input  sign,
  input  en,
  output [3:0] anode,
  output [7:0] hseg
);

  wire wclk;
  wire [3:0] register_1_q, ring4_1_q;
  wire [7:0] register_2_q, SEGROM_data;

  not not_1 (wclk, clk);
  ROM #(.addrWidth(13)) SEGROM (.addr({1'b0, ring4_1_q, value}), .data(SEGROM_data));
  ring4 ring4_1 (.Q(ring4_1_q), .clr(reset), .clk(clk));
  Register #(.width(4)) register_1 (.D(ring4_1_q), .en(en), .clk(wclk), .Q(register_1_q));  // open: clr
  Register register_2 (.D(SEGROM_data), .en(en), .clk(wclk), .Q(register_2_q));  // open: clr
  assign anode = en ? register_1_q : 4'bz;  // Controlled_Buffer controlled_buffer_1
  assign hseg = en ? register_2_q : 8'bz;  // Controlled_Buffer controlled_buffer_2

  // Other names for the same wires on the sheet: clr = reset; sgn = sign

  // Notes on the sheet:
  //   contents of SEGROM (hex, n*v repeats v):
  //   256*0 7e 12 bc b6 d2 e6 ee 32 fe f2 7e 12 bc b6 d2 e6 ee 32 fe f2 7e 12 bc b6 d2 e6 ee 32 fe f2 7e
  //   12 bc b6 d2 e6 ee 32 fe f2 7e 12 bc b6 d2 e6 ee 32 fe f2 7e 12 bc b6 d2 e6 ee 32 fe f2 7e 12 bc b6
  //   d2 e6 ee 32 fe f2 7e 12 bc b6 d2 e6 ee 32 fe f2 7e 12 bc b6 d2 e6 ee 32 fe f2 7e 12 bc b6 d2 e6 ee
  //   32 fe f2 7e 12 bc b6 d2 e6 ee 32 fe f2 7e 12 bc b6 d2 e6 ee 32 fe f2 7e 12 bc b6 d2 e6 ee 32 fe f2
  //   7e 12 bc b6 d2 e6 ee 32 fe f2 7e 12 bc b6 d2 e6 ee 32 fe f2 7e 12 bc b6 d2 e6 ee 32 fe f2 7e 12 bc
  //   b6 d2 e6 ee 32 fe f2 7e 12 bc b6 d2 e6 ee 32 fe f2 7e 12 bc b6 d2 e6 ee 32 fe f2 7e 12 bc b6 d2 e6
  //   ee 32 fe f2 7e 12 bc b6 d2 e6 ee 32 fe f2 7e 12 bc b6 d2 e6 ee 32 fe f2 7e 12 bc b6 d2 e6 ee 32 fe
  //   f2 7e 12 bc b6 d2 e6 ee 32 fe f2 7e 12 bc b6 d2 e6 ee 32 fe f2 7e 12 bc b6 d2 e6 10*0 10*12 10*bc
  //   10*b6 10*d2 10*e6 10*ee 10*32 10*fe 10*f2 10*7e 10*12 10*bc 10*b6 10*d2 10*e6 10*ee 10*32 10*fe
  //   10*f2 10*7e 10*12 10*bc 10*b6 10*d2 6*e6 6*1 10*ff 340*0 100*12 56*bc
endmodule

module debounce (
  input  req,
  input  clk,
  output resp
);

  wire d_ff_1_q, d_ff_1_qn, d_ff_2_qn;

  D_Flip_Flop d_ff_1 (.D(req), .clk(clk), .Q(d_ff_1_q), .Qn(d_ff_1_qn));  // open: preset, reset
  D_Flip_Flop d_ff_2 (.D(d_ff_1_q), .clk(clk), .Qn(d_ff_2_qn));  // open: Q, preset, reset
  D_Flip_Flop d_ff_3 (.D(d_ff_2_qn), .clk(clk), .Qn(resp));  // open: Q, preset, reset
endmodule

module toggleswitch (
  input  I,
  input  clk,
  input  res,
  output switch,
  output latch
);

  wire d_ff_1_q, d_ff_2_qn;

  D_Flip_Flop d_ff_1 (.D(I), .clk(clk), .Q(d_ff_1_q), .reset(res));  // open: Qn, preset
  D_Flip_Flop d_ff_2 (.D(d_ff_2_qn), .clk(d_ff_1_q), .Q(switch), .Qn(d_ff_2_qn), .reset(res));  // open: preset
  D_Flip_Flop d_ff_3 (.D(d_ff_1_q), .clk(clk), .Q(latch), .reset(res));  // open: Qn, preset
endmodule

// ALU
module alu (
  input  cin,
  input  [7:0] A,
  input  [7:0] B,
  input  en,
  input  [5:0] fn,
  output [7:0] res,
  output C,
  output Z,
  output P,
  output V
);

  wire and_2_out, and_3_out, and_4_out, cia, coa, cos, not_1_out, not_2_out, not_3_out, not_shift,
       Subtract_Function;
  wire [3:0] or_1_out;
  wire [7:0] aunit_s, lunit_res, sunit_res;

  not not_1 (not_1_out, fn[2]);
  not not_2 (not_2_out, fn[3]);
  shiftunit sunit (.res(sunit_res), .cout(cos), .A(A), .sfn(fn[5:4]), .cin(cin));
  logicunit lunit (.Res(lunit_res), .B(B), .A(A), .lfnc(fn[3:0]));
  xnor xnor_1 (not_shift, fn[4], fn[5]);
  and and_1 (Subtract_Function, fn[0], fn[1], not_1_out, not_2_out);
  adderunit aunit (.cout(coa), .S(aunit_s), .B(lunit_res), .A(sunit_res), .cin(cia));
  alures aluflags (.V(or_1_out[3]), .P(or_1_out[2]), .Z(or_1_out[1]), .aMSB(A[7]), .bMSB(B[7]), .ares(aunit_s));
  assign res = en ? aunit_s : 8'bz;  // Controlled_Buffer controlled_buffer_1
  assign {V, P, Z, C} = en ? or_1_out : 4'bz;  // Controlled_Buffer controlled_buffer_2
  and and_2 (and_2_out, not_shift, coa);
  or or_1 (or_1_out[0], and_2_out, and_3_out);
  not not_3 (not_3_out, not_shift);
  and and_3 (and_3_out, not_3_out, cos);
  and and_4 (and_4_out, cos, not_shift);
  or or_2 (cia, Subtract_Function, and_4_out);

  // Other names for the same wires on the sheet: aMSB = A[7]; bMSB = B[7]; enable = en; f0 = fn[0];
  //   lfn[3:0] = fn[3:0]; f1 = fn[1]; f2 = fn[2]; f3 = fn[3]; f4 = fn[4]; sfn[1:0] = fn[5:4]; f5 = fn[5]

  // Notes on the sheet:
  //   Valid functions fn
  //   ADD 001100
  //   SUB  000011
  //   AND  111000
  //   OR   111110
  //   XOR  110110
  //   SHR  010000
  //   SHR  100000
  //   The 'NOT B' logic function is used for 'Subtract'
  //   We need to set Carry if this is the case
  //   If we are executing SHR or SHL we need to ignore carry results from ADDER unit
endmodule

module adderunit (
  input  [7:0] A,
  input  [7:0] B,
  input  cin,
  output cout,
  output [7:0] S
);

  wire c0, c1, c2, c3, c4, c5, c6;

  fulladder fulladder_1 (.S(S[0]), .Co(c0), .A(A[0]), .B(B[0]), .Ci(cin));
  fulladder fulladder_2 (.S(S[1]), .Co(c1), .A(A[1]), .B(B[1]), .Ci(c0));
  fulladder fulladder_3 (.S(S[2]), .Co(c2), .A(A[2]), .B(B[2]), .Ci(c1));
  fulladder fulladder_4 (.S(S[3]), .Co(c3), .A(A[3]), .B(B[3]), .Ci(c2));
  fulladder fulladder_5 (.S(S[4]), .Co(c4), .A(A[4]), .B(B[4]), .Ci(c3));
  fulladder fulladder_6 (.S(S[5]), .Co(c5), .A(A[5]), .B(B[5]), .Ci(c4));
  fulladder fulladder_7 (.S(S[6]), .Co(c6), .A(A[6]), .B(B[6]), .Ci(c5));
  fulladder fulladder_8 (.S(S[7]), .Co(cout), .A(A[7]), .B(B[7]), .Ci(c6));

  // Other names for the same wires on the sheet: c7 = cout

  // Notes on the sheet:
  //   8-Bit Adder with Carry In
endmodule

module logicunit (
  input  [7:0] B,
  input  [7:0] A,
  input  [3:0] lfnc,
  output [7:0] Res
);

  wire en;

  Multiplexer #(.select(2)) multiplexer_1 (
    .in0(lfnc[0]), .in1(lfnc[1]), .in2(lfnc[2]), .in3(lfnc[3]), .out(Res[0]), .sel({B[0], A[0]}), .en(en));
  Multiplexer #(.select(2)) multiplexer_2 (
    .in0(lfnc[0]), .in1(lfnc[1]), .in2(lfnc[2]), .in3(lfnc[3]), .out(Res[1]), .sel({B[1], A[1]}), .en(en));
  Multiplexer #(.select(2)) multiplexer_3 (
    .in0(lfnc[0]), .in1(lfnc[1]), .in2(lfnc[2]), .in3(lfnc[3]), .out(Res[2]), .sel({B[2], A[2]}), .en(en));
  Multiplexer #(.select(2)) multiplexer_4 (
    .in0(lfnc[0]), .in1(lfnc[1]), .in2(lfnc[2]), .in3(lfnc[3]), .out(Res[3]), .sel({B[3], A[3]}), .en(en));
  Multiplexer #(.select(2)) multiplexer_5 (
    .in0(lfnc[0]), .in1(lfnc[1]), .in2(lfnc[2]), .in3(lfnc[3]), .out(Res[4]), .sel({B[4], A[4]}), .en(en));
  Multiplexer #(.select(2)) multiplexer_6 (
    .in0(lfnc[0]), .in1(lfnc[1]), .in2(lfnc[2]), .in3(lfnc[3]), .out(Res[5]), .sel({B[5], A[5]}), .en(en));
  Multiplexer #(.select(2)) multiplexer_7 (
    .in0(lfnc[0]), .in1(lfnc[1]), .in2(lfnc[2]), .in3(lfnc[3]), .out(Res[6]), .sel({B[6], A[6]}), .en(en));
  Multiplexer #(.select(2)) multiplexer_8 (
    .in0(lfnc[0]), .in1(lfnc[1]), .in2(lfnc[2]), .in3(lfnc[3]), .out(Res[7]), .sel({B[7], A[7]}), .en(en));

  // Other names for the same wires on the sheet: fnc[3:0] = lfnc; r0 = Res[0]; r1 = Res[1]; r2 = Res[2]; r3 = Res[3];
  //   r4 = Res[4]; r5 = Res[5]; r6 = Res[6]; r7 = Res[7]

  // Notes on the sheet:
  //   LOGIC Units Made out of MUXes
  //   0xa          A
  //   0xc          B
  //   0x8          AND
  //   0xe          OR
  //   0x6          XOR
  //   0x1          NOR
  //   0xf          255
  //   lfnc         Logic Function
  //   0x7          NAND
  //   0x3          NOT B
  //   0x5          NOT A
  //   0x0         Zero (0)
endmodule

module shiftunit (
  input  [7:0] A,
  input  [1:0] sfn,
  input  cin,
  output [7:0] res,
  output cout
);

  wire en;

  Multiplexer #(.select(2)) multiplexer_1 (
    .in0(A[0]), .in1(A[1]), .in2(cin), .in3(1'b0), .out(res[0]), .sel(sfn), .en(en));
  Multiplexer #(.select(2)) multiplexer_2 (
    .in0(A[4]), .in1(A[5]), .in2(A[3]), .in3(1'b0), .out(res[4]), .sel(sfn), .en(en));
  Multiplexer #(.select(2)) multiplexer_3 (
    .in0(A[1]), .in1(A[2]), .in2(A[0]), .in3(1'b0), .out(res[1]), .sel(sfn), .en(en));
  Multiplexer #(.select(2)) multiplexer_4 (
    .in0(A[5]), .in1(A[6]), .in2(A[4]), .in3(1'b0), .out(res[5]), .sel(sfn), .en(en));
  Multiplexer #(.select(2)) multiplexer_5 (
    .in0(cin), .in1(A[0]), .in2(A[7]), .in3(1'b0), .out(cout), .sel(sfn), .en(en));
  Multiplexer #(.select(2)) multiplexer_6 (
    .in0(A[2]), .in1(A[3]), .in2(A[1]), .in3(1'b0), .out(res[2]), .sel(sfn), .en(en));
  Multiplexer #(.select(2)) multiplexer_7 (
    .in0(A[6]), .in1(A[7]), .in2(A[5]), .in3(1'b0), .out(res[6]), .sel(sfn), .en(en));
  Multiplexer #(.select(2)) multiplexer_8 (
    .in0(A[3]), .in1(A[4]), .in2(A[2]), .in3(1'b0), .out(res[3]), .sel(sfn), .en(en));
  Multiplexer #(.select(2)) multiplexer_9 (
    .in0(A[7]), .in1(cin), .in2(A[6]), .in3(1'b0), .out(res[7]), .sel(sfn), .en(en));

  // Other names for the same wires on the sheet: r0 = res[0]; r1 = res[1]; r2 = res[2]; r3 = res[3]; r4 = res[4];
  //   r5 = res[5]; r6 = res[6]; r7 = res[7]; sfnc[1:0] = sfn

  // Notes on the sheet:
  //   sfnc         Shift Function
  //   b00          no change
  //   b01          Shift Right
  //   b10          Shift Left
  //   b11          Clear
endmodule

module fulladder (
  input  A,
  input  B,
  input  Ci,
  output S,
  output Co
);

  wire and_1_out, and_2_out, and_3_out, or_1_out, xor_1_out;

  xor xor_1 (xor_1_out, A, B);
  and and_1 (and_1_out, A, B);
  and and_2 (and_2_out, A, Ci);
  and and_3 (and_3_out, B, Ci);
  or or_1 (or_1_out, and_1_out, and_2_out);
  xor xor_2 (S, xor_1_out, Ci);
  or or_2 (Co, or_1_out, and_3_out);

  // Notes on the sheet:
  //   Full 1-bit Adder (carry In, A, B) --> (S(um), carry out)
endmodule

module alures (
  input  [7:0] ares,
  input  aMSB,
  input  bMSB,
  output Z,
  output P,
  output V
);

  wire or_1_out, or_2_out, or_3_out, or_4_out, or_5_out, or_6_out, xor_1_out, xor_2_out, xor_3_out,
       xor_4_out, xor_5_out, xor_6_out, xor_7_out, xor_8_out;

  xor xor_1 (xor_1_out, aMSB, ares[7]);
  xor xor_2 (xor_2_out, ares[7], bMSB);
  and and_1 (V, xor_1_out, xor_2_out);
  or or_1 (or_1_out, ares[7], ares[6]);
  or or_2 (or_2_out, ares[5], ares[4]);
  or or_3 (or_3_out, ares[3], ares[2]);
  or or_4 (or_4_out, ares[1], ares[0]);
  xor xor_3 (xor_3_out, ares[7], ares[6]);
  xor xor_4 (xor_4_out, ares[5], ares[4]);
  xor xor_5 (xor_5_out, ares[3], ares[2]);
  xor xor_6 (xor_6_out, ares[1], ares[0]);
  or or_5 (or_5_out, or_1_out, or_2_out);
  or or_6 (or_6_out, or_3_out, or_4_out);
  xor xor_7 (xor_7_out, xor_3_out, xor_4_out);
  xor xor_8 (xor_8_out, xor_5_out, xor_6_out);
  nor nor_1 (Z, or_5_out, or_6_out);
  xor xor_9 (P, xor_7_out, xor_8_out);

  // Other names for the same wires on the sheet: r0 = ares[0]; r1 = ares[1]; r2 = ares[2]; r3 = ares[3]; r4 = ares[4];
  //   r5 = ares[5]; r6 = ares[6]; r7 = ares[7]; Overflow = V; ParityOdd = P; Zero = Z
endmodule

module ring6 (
  input  clr,
  input  clk,
  output [5:0] Q
);

  wire q6, q7;

  D_Flip_Flop d_ff_1 (.D(q6), .clk(clk), .Q(q7), .reset(clr));  // open: Qn, preset
  D_Flip_Flop d_ff_2 (.D(Q[5]), .clk(clk), .Q(q6), .reset(clr));  // open: Qn, preset
  D_Flip_Flop d_ff_3 (.D(Q[4]), .clk(clk), .Q(Q[5]), .reset(clr));  // open: Qn, preset
  D_Flip_Flop d_ff_4 (.D(Q[3]), .clk(clk), .Q(Q[4]), .reset(clr));  // open: Qn, preset
  D_Flip_Flop d_ff_5 (.D(Q[2]), .clk(clk), .Q(Q[3]), .reset(clr));  // open: Qn, preset
  D_Flip_Flop d_ff_6 (.D(Q[1]), .clk(clk), .Q(Q[2]), .reset(clr));  // open: Qn, preset
  D_Flip_Flop d_ff_7 (.D(Q[0]), .clk(clk), .Q(Q[1]), .reset(clr));  // open: Qn, preset
  D_Flip_Flop d_ff_8 (.D(Q[5]), .clk(clk), .Q(Q[0]), .preset(clr));  // open: Qn, reset
endmodule

// PC
module pcreg (
  input  reset,
  input  load,
  input  counten,
  input  clk,
  input  [15:0] Din,
  input  pcout,
  output [15:0] dbg,
  output [15:0] Dout
);

  wire not_1_out;

  Counter #(.max('hffff), .width(16)) counter_1 (
    .clr(reset), .load(load), .up(1'b1), .count(counten), .clk(clk), .D(Din), .Q(dbg));  // open: carry
  not not_1 (not_1_out, pcout);
  Pull_Resistor pull_resistor_1 (.node(pcout));
  assign Dout = not_1_out ? dbg : 16'bz;  // Controlled_Buffer controlled_buffer_1
endmodule

// PC-4bit
module pcreg4 (
  input  reset,
  input  load,
  input  counten,
  input  clk,
  input  [15:0] Din,
  input  pcout,
  output [15:0] dbg,
  output [15:0] Dout
);

  wire not_1_out;
  wire [3:0] counter_1_q;

  Counter #(.max('hf), .width(4)) counter_1 (
    .clr(reset), .load(load), .up(1'b1), .count(counten), .clk(clk), .D(Din[3:0]), .Q(counter_1_q));  // open: carry
  assign dbg = {{12{1'b0}}, counter_1_q};  // Bit_Extender bit_extender_1
  assign Dout = not_1_out ? dbg : 16'bz;  // Controlled_Buffer controlled_buffer_1
  not not_1 (not_1_out, pcout);
  Pull_Resistor pull_resistor_1 (.node(pcout));
endmodule

module reg8bank (
  input  clk,
  input  [7:0] I,
  input  [2:0] regsel,
  input  [7:0] weMask,
  input  res,
  input  en,
  output [7:0] Q
);

  wire en0, en1, en2, en3, en4, en5, en6, en7, we5;
  wire [7:0] bankout, register_1_q, register_2_q, register_3_q, register_4_q, register_5_q, register_6_q,
       register_7_q, register_8_q;

  Decoder #(.select(3)) decoder_1 (
    .out0(en0), .out1(en1), .out2(en2), .out3(en3), .out4(en4), .out5(en5), .out6(en6), .out7(en7),
    .sel(regsel));  // open: en
  Register register_1 (.D(I), .en(weMask[0]), .clk(clk), .Q(register_1_q), .clr(res));
  Pull_Resistor pull_resistor_1 (.node(en0));
  Register register_2 (.D(I), .en(weMask[2]), .clk(clk), .Q(register_2_q), .clr(res));
  Register register_3 (.D(I), .en(weMask[5]), .clk(clk), .Q(register_3_q), .clr(res));
  Register register_4 (.D(I), .en(weMask[6]), .clk(clk), .Q(register_4_q), .clr(res));
  assign bankout = en0 ? register_1_q : 8'bz;  // Controlled_Buffer controlled_buffer_1
  assign bankout = en2 ? register_2_q : 8'bz;  // Controlled_Buffer controlled_buffer_2
  Pull_Resistor pull_resistor_2 (.node(en2));
  assign bankout = en4 ? register_3_q : 8'bz;  // Controlled_Buffer controlled_buffer_3
  Pull_Resistor pull_resistor_3 (.node(en4));
  assign bankout = en6 ? register_4_q : 8'bz;  // Controlled_Buffer controlled_buffer_4
  Pull_Resistor pull_resistor_4 (.node(en6));
  Register register_5 (.D(I), .en(weMask[1]), .clk(clk), .Q(register_5_q), .clr(res));
  Register register_6 (.D(I), .en(weMask[3]), .clk(clk), .Q(register_6_q), .clr(res));
  Register register_7 (.D(I), .en(we5), .clk(clk), .Q(register_7_q), .clr(res));
  Register register_8 (.D(I), .en(weMask[7]), .clk(clk), .Q(register_8_q), .clr(res));
  assign bankout = en1 ? register_5_q : 8'bz;  // Controlled_Buffer controlled_buffer_5
  Pull_Resistor pull_resistor_5 (.node(en1));
  assign bankout = en3 ? register_6_q : 8'bz;  // Controlled_Buffer controlled_buffer_6
  Pull_Resistor pull_resistor_6 (.node(en3));
  assign bankout = en5 ? register_7_q : 8'bz;  // Controlled_Buffer controlled_buffer_7
  Pull_Resistor pull_resistor_7 (.node(en5));
  assign bankout = en7 ? register_8_q : 8'bz;  // Controlled_Buffer controlled_buffer_8
  Pull_Resistor pull_resistor_8 (.node(en7));
  assign Q = en ? bankout : 8'bz;  // Controlled_Buffer controlled_buffer_9
  Pull_Resistor pull_resistor_9 (.node(en));

  assign weMask[4] = weMask[5];

  // Other names for the same wires on the sheet: dataIn[7:0] = I; reset = res; selreg[2:0] = regsel; we0 = weMask[0];
  //   we1 = weMask[1]; we2 = weMask[2]; we3 = weMask[3]; we4 = weMask[5]; we6 = weMask[6]; we7 = weMask[7]

  // Notes on the sheet:
  //   8 Bank 8-bit Registers multi select on writing
endmodule

module reg4bank (
  input  clk,
  input  [7:0] I,
  input  [1:0] regsel,
  input  [3:0] weMask,
  input  res,
  input  en,
  output [7:0] Q
);

  wire en0, en1, en2, en3;
  wire [7:0] bankout, register_1_q, register_2_q, register_3_q, register_4_q;

  Decoder #(.select(2)) decoder_1 (.out0(en0), .out1(en1), .out2(en2), .out3(en3), .sel(regsel));  // open: en
  Register register_1 (.D(I), .en(weMask[0]), .clk(clk), .Q(register_1_q), .clr(res));
  Pull_Resistor pull_resistor_1 (.node(en0));
  Register register_2 (.D(I), .en(weMask[2]), .clk(clk), .Q(register_2_q), .clr(res));
  assign bankout = en0 ? register_1_q : 8'bz;  // Controlled_Buffer controlled_buffer_1
  assign bankout = en2 ? register_2_q : 8'bz;  // Controlled_Buffer controlled_buffer_2
  Pull_Resistor pull_resistor_2 (.node(en2));
  Register register_3 (.D(I), .en(weMask[1]), .clk(clk), .Q(register_3_q), .clr(res));
  Register register_4 (.D(I), .en(weMask[3]), .clk(clk), .Q(register_4_q), .clr(res));
  assign bankout = en1 ? register_3_q : 8'bz;  // Controlled_Buffer controlled_buffer_3
  Pull_Resistor pull_resistor_3 (.node(en1));
  assign bankout = en3 ? register_4_q : 8'bz;  // Controlled_Buffer controlled_buffer_4
  Pull_Resistor pull_resistor_4 (.node(en3));
  assign Q = en ? bankout : 8'bz;  // Controlled_Buffer controlled_buffer_5
  Pull_Resistor pull_resistor_5 (.node(en));

  // Other names for the same wires on the sheet: dataIn[7:0] = I; reset = res; selreg[1:0] = regsel; we0 = weMask[0];
  //   we1 = weMask[1]; we2 = weMask[2]; we3 = weMask[3]

  // Notes on the sheet:
  //   4 Bank 8-bit Registers multi select on writing
endmodule

module constantbank (
  input  [2:0] regsel,
  input  en,
  output [7:0] Q
);

  wire en0, en1, en2, en3, en4, en5, en6, en7;
  wire [7:0] bankout;

  Decoder #(.select(3)) decoder_1 (
    .out0(en0), .out1(en1), .out2(en2), .out3(en3), .out4(en4), .out5(en5), .out6(en6), .out7(en7),
    .sel(regsel));  // open: en
  assign bankout = en0 ? {8{1'b0}} : 8'bz;  // Controlled_Buffer controlled_buffer_1
  assign bankout = en1 ? 8'h1 : 8'bz;  // Controlled_Buffer controlled_buffer_2
  assign bankout = en2 ? 8'h2 : 8'bz;  // Controlled_Buffer controlled_buffer_3
  assign bankout = en3 ? 8'h4 : 8'bz;  // Controlled_Buffer controlled_buffer_4
  assign bankout = en4 ? 8'h10 : 8'bz;  // Controlled_Buffer controlled_buffer_5
  assign bankout = en5 ? 8'hf0 : 8'bz;  // Controlled_Buffer controlled_buffer_6
  assign bankout = en6 ? 8'hf : 8'bz;  // Controlled_Buffer controlled_buffer_7
  assign bankout = en7 ? {8{1'b1}} : 8'bz;  // Controlled_Buffer controlled_buffer_8
  Pull_Resistor pull_resistor_1 (.node(en));
  assign Q = en ? bankout : 8'bz;  // Controlled_Buffer controlled_buffer_9

  // Other names for the same wires on the sheet: selreg[2:0] = regsel
endmodule

module rammodule (
  input  [15:0] addr,
  input  we,
  input  oe,
  input  clk,
  input  [7:0] din,
  output [7:0] dout
);

  wire [7:0] ram_1_dout;

  RAM #(.addrWidth(16), .\type ("nonvolatile")) ram_1 (
    .addr(addr), .we(we), .oe(oe), .clk(clk), .din(din), .dout(ram_1_dout));
  assign dout = oe ? ram_1_dout : 8'bz;  // Controlled_Buffer controlled_buffer_1
endmodule

module bcd7seg (
  input  [3:0] value,
  input  en,
  output a,
  output b,
  output c,
  output d,
  output e,
  output f,
  output g,
  output dp
);

  wire AorB, as, bs, cs, ds, es, fs, gs, nA, nB, nC, nD;

  or or_1 (AorB, value[3], value[2]);
  or or_2 (cs, nC, value[0], value[2]);
  not not_1 (nA, value[3]);
  not not_2 (nB, value[2]);
  not not_3 (nC, value[1]);
  not not_4 (nD, value[0]);
  Multiplexer #(.enable("false"), .select(2)) multiplexer_1 (
    .in0(nB), .in1(AorB), .in2(nB), .in3(1'b1), .out(as), .sel(value[1:0]));
  Multiplexer #(.enable("false"), .select(2)) multiplexer_2 (
    .in0(1'b1), .in1(nB), .in2(nB), .in3(1'b1), .out(bs), .sel(value[1:0]));
  Multiplexer #(.enable("false"), .select(2)) multiplexer_3 (
    .in0(nB), .in1(value[2]), .in2(1'b1), .in3(nB), .out(ds), .sel(value[1:0]));
  Multiplexer #(.enable("false"), .select(2)) multiplexer_4 (
    .in0(nB), .in1(1'b0), .in2(1'b1), .in3(1'b0), .out(es), .sel(value[1:0]));
  Multiplexer #(.enable("false"), .select(2)) multiplexer_5 (
    .in0(1'b1), .in1(AorB), .in2(value[2]), .in3(1'b0), .out(fs), .sel(value[1:0]));
  Multiplexer #(.enable("false"), .select(2)) multiplexer_6 (
    .in0(AorB), .in1(AorB), .in2(1'b1), .in3(nB), .out(gs), .sel(value[1:0]));
  assign a = en ? as : 1'bz;  // Controlled_Buffer controlled_buffer_1
  assign b = en ? bs : 1'bz;  // Controlled_Buffer controlled_buffer_2
  assign c = en ? cs : 1'bz;  // Controlled_Buffer controlled_buffer_3
  assign d = en ? ds : 1'bz;  // Controlled_Buffer controlled_buffer_4
  assign e = en ? es : 1'bz;  // Controlled_Buffer controlled_buffer_5
  assign f = en ? fs : 1'bz;  // Controlled_Buffer controlled_buffer_6
  assign g = en ? gs : 1'bz;  // Controlled_Buffer controlled_buffer_7
  assign dp = en ? 1'b0 : 1'bz;  // Controlled_Buffer controlled_buffer_8

  // Other names for the same wires on the sheet: D_t = value[0]; sel[1:0] = value[1:0]; C_t = value[1];
  //   B_t = value[2]; A_t = value[3]

  // Notes on the sheet:
  //   BCD - 7-Seg Display Driver
  //   Digital Logic and Computer Organisation - RAJARAMAN et al - Johnny Brighton 2021
endmodule

module hex7seg (
  input  [3:0] value,
  input  dot,
  input  en,
  output a,
  output b,
  output c,
  output d,
  output e,
  output f,
  output g,
  output dp
);

  wire as, bs, cs, ds, es, fs, gs;
  wire [7:7] rom_1_data;

  ROM #(.addrWidth(4)) rom_1 (.addr(value), .data({rom_1_data[7], gs, fs, es, ds, cs, bs, as}));
  assign a = en ? as : 1'bz;  // Controlled_Buffer controlled_buffer_1
  assign b = en ? bs : 1'bz;  // Controlled_Buffer controlled_buffer_2
  assign c = en ? cs : 1'bz;  // Controlled_Buffer controlled_buffer_3
  assign d = en ? ds : 1'bz;  // Controlled_Buffer controlled_buffer_4
  assign e = en ? es : 1'bz;  // Controlled_Buffer controlled_buffer_5
  assign f = en ? fs : 1'bz;  // Controlled_Buffer controlled_buffer_6
  assign g = en ? gs : 1'bz;  // Controlled_Buffer controlled_buffer_7
  assign dp = en ? dot : 1'bz;  // Controlled_Buffer controlled_buffer_8

  // Other names for the same wires on the sheet: dp_t = dot

  // Notes on the sheet:
  //   contents of rom_1 (hex, n*v repeats v):
  //   3f 6 5b 4f 66 6d 7d 7 7f 6f 77 7c 39 5e 79 71
  //   HEX - 7-Seg Display Driver
  //   0:0x3f, 1:0x06, 2:0x5b, 3:0x4f, 4:0x66, 5:0x6d, 6:0x7d, 7:0x07, 8:7f, 9:0x6f, 10:0x77, 11:0x7c, 12:0x39, 13:0x5e, 14:0x79, 15:0x71
endmodule

module seg16hdisplay (
  input  reset,
  input  clk,
  input  [15:0] I,
  input  en,
  output [3:0] anode,
  output [7:0] hseg
);

  wire a, b, c, d, e, f, g, p, wclk;
  wire [3:0] nybble, Q;

  not not_1 (wclk, clk);
  assign nybble = Q[0] ? I[3:0] : 4'bz;  // Controlled_Buffer controlled_buffer_1
  assign nybble = Q[2] ? I[11:8] : 4'bz;  // Controlled_Buffer controlled_buffer_2
  assign nybble = Q[1] ? I[7:4] : 4'bz;  // Controlled_Buffer controlled_buffer_3
  assign nybble = Q[3] ? I[15:12] : 4'bz;  // Controlled_Buffer controlled_buffer_4
  hex7seg hex7seg_1 (.a(a), .b(b), .c(c), .d(d), .e(e), .f(f), .g(g), .dp(p), .en(en), .value(nybble));  // open: dot
  ring4 ring4_1 (.Q(Q), .clr(reset), .clk(clk));
  assign anode = en ? Q : 4'bz;  // Controlled_Buffer controlled_buffer_5
  assign hseg = en ? {g, f, a, b, e, d, c, p} : 8'bz;  // Controlled_Buffer controlled_buffer_6

  // Other names for the same wires on the sheet: clr = reset; Q1 = Q[0]; Q2 = Q[1]; Q3 = Q[2]; Q4 = Q[3];
  //   value16[15:0] = I
endmodule

module TESTaltHexDisplay (
);

  wire cpuCLKdiv2, H1, H2, H3, H4, uRESET;
  wire [3:0] b1s, b2s, b3s, b4s, bs, t1s, t2s, t3s, t4s, ts;

  _7_Segment_Display u_7_segment_display_1 (
    .g(t4s[3]), .f(t4s[2]), .a(t4s[1]), .b(t4s[0]), .e(b4s[3]), .d(b4s[2]), .c(b4s[1]), .dp(b4s[0]));
  _7_Segment_Display u_7_segment_display_2 (
    .g(t3s[3]), .f(t3s[2]), .a(t3s[1]), .b(t3s[0]), .e(b3s[3]), .d(b3s[2]), .c(b3s[1]), .dp(b3s[0]));
  _7_Segment_Display u_7_segment_display_3 (
    .g(t2s[3]), .f(t2s[2]), .a(t2s[1]), .b(t2s[0]), .e(b2s[3]), .d(b2s[2]), .c(b2s[1]), .dp(b2s[0]));
  _7_Segment_Display u_7_segment_display_4 (
    .g(t1s[3]), .f(t1s[2]), .a(t1s[1]), .b(t1s[0]), .e(b1s[3]), .d(b1s[2]), .c(b1s[1]), .dp(b1s[0]));
  // Probe on {H4, H3, H2, H1}
  assign t1s = H1 ? ts : 4'bz;  // Controlled_Buffer controlled_buffer_1
  assign b1s = H1 ? bs : 4'bz;  // Controlled_Buffer controlled_buffer_2
  seg16hdisplay seg16hdisplay_1 (
    .anode({H4, H3, H2, H1}), .hseg({ts, bs}), .I(16'h1234), .en(1'b1), .reset(uRESET), .clk(cpuCLKdiv2));
  // Probe on {ts, bs}
  assign t2s = H2 ? ts : 4'bz;  // Controlled_Buffer controlled_buffer_3
  assign b2s = H2 ? bs : 4'bz;  // Controlled_Buffer controlled_buffer_4
  assign t3s = H3 ? ts : 4'bz;  // Controlled_Buffer controlled_buffer_5
  assign b3s = H3 ? bs : 4'bz;  // Controlled_Buffer controlled_buffer_6
  assign t4s = H4 ? ts : 4'bz;  // Controlled_Buffer controlled_buffer_7
  assign b4s = H4 ? bs : 4'bz;  // Controlled_Buffer controlled_buffer_8
endmodule

module TESTALU (
  input  in_1,
  input  [7:0] in_2,
  input  [7:0] in_3,
  input  [5:0] in_4,
  input  [2:0] in_5,
  output [7:0] out_6
);

  wire alu_1_c, alu_1_p, alu_1_v, alu_1_z, and_1_out, and_2_out, and_3_out, and_4_out, and_5_out, and_6_out,
       and_7_out, and_8_out, pull_resistor_1_node;
  wire [5:0] alufnc;

  Pull_Resistor #(.pull(1)) pull_resistor_1 (.node(pull_resistor_1_node));
  // Probe on in_2
  // Probe on in_3
  and and_1 (and_1_out, ~alufnc[5], ~alufnc[4], alufnc[3], alufnc[2], ~alufnc[1], ~alufnc[0]);  // AND_Gate
  LED led_1 (.in(and_1_out));
  LED led_2 (.in(pull_resistor_1_node));
  alu alu_1 (
    .res(out_6), .C(alu_1_c), .Z(alu_1_z), .P(alu_1_p), .V(alu_1_v), .A(in_2), .B(in_3), .fn(alufnc),
    .cin(in_1), .en(1'b1));
  and and_2 (and_2_out, ~alufnc[5], ~alufnc[4], ~alufnc[3], ~alufnc[2], alufnc[1], alufnc[0]);  // AND_Gate
  LED led_3 (.in(and_2_out));
  // Probe on out_6
  LED led_4 (.in(alu_1_c));
  LED led_5 (.in(alu_1_z));
  LED led_6 (.in(alu_1_p));
  LED led_7 (.in(alu_1_v));
  and and_3 (and_3_out, alufnc[5], ~alufnc[4], ~alufnc[3], ~alufnc[2], ~alufnc[1], ~alufnc[0]);  // AND_Gate
  LED led_8 (.in(and_3_out));
  and and_4 (and_4_out, ~alufnc[5], alufnc[4], ~alufnc[3], ~alufnc[2], ~alufnc[1], ~alufnc[0]);  // AND_Gate
  LED led_9 (.in(and_4_out));
  and and_5 (and_5_out, alufnc[5], alufnc[4], alufnc[3], ~alufnc[2], ~alufnc[1], ~alufnc[0]);  // AND_Gate
  LED led_10 (.in(and_5_out));
  and and_6 (and_6_out, alufnc[5], alufnc[4], alufnc[3], alufnc[2], alufnc[1], ~alufnc[0]);  // AND_Gate
  LED led_11 (.in(and_6_out));
  and and_7 (and_7_out, alufnc[5], alufnc[4], ~alufnc[3], alufnc[2], alufnc[1], ~alufnc[0]);  // AND_Gate
  LED led_12 (.in(and_7_out));
  // Probe on alufnc
  Multiplexer #(.enable("false"), .select(3), .width(6)) multiplexer_1 (
    .in0(6'b001100), .in1(6'b000011), .in2(6'b100000), .in3(6'b010000), .in4(6'b111000), .in5(6'b111110),
    .in6(6'b110110), .in7({6{1'b0}}), .out(alufnc), .sel(in_5));
  and and_8 (and_8_out, ~alufnc[5], ~alufnc[4], ~alufnc[3], ~alufnc[2], ~alufnc[1], ~alufnc[0]);  // AND_Gate
  LED led_13 (.in(and_8_out));

  // Other names for the same wires on the sheet: fncsel[2:0] = in_5

  // Notes on the sheet:
  //   ADD
  //   SUB
  //   SHIFT LEFT
  //   SHIFT RIGHT
  //   AND
  //   OR
  //   XOR
  //   NOP
endmodule
